// Logisim project csproject-no shift.circ as structural Verilog: 11 circuits, main circuit main
module main (
  input  in_1,
  input  in_2,
  input  in_3,
  input  in_4,
  input  in_5,
  input  in_6,
  input  in_7,
  input  in_8,
  input  in_9,
  input  in_10,
  input  in_11,
  input  in_12,
  input  in_13,
  input  in_14,
  input  in_15,
  input  in_16,
  input  in_17,
  input  in_18,
  input  in_19,
  input  in_20,
  input  in_21,
  input  in_22,
  input  in_23,
  input  in_24,
  input  in_25,
  input  in_26,
  input  in_27,
  input  in_28,
  input  in_29,
  input  in_30,
  output overflow,
  output out_32,
  output out_33,
  output out_34,
  output out_35,
  output out_36,
  output out_37,
  output out_38,
  output out_39,
  output out_40,
  output out_41,
  output out_42,
  output out_43,
  output out_44,
  output out_45,
  output out_46,
  output out_47,
  output out_48,
  output out_49,
  output out_50,
  output out_51,
  output out_52
);

  wire mantissa_1_out_13;

  sign sign_1 (.in_1(in_1), .in_2(in_10), .out_3(out_32));
  exponent exponent_1 (
    .A0(in_9), .B0(in_18), .A1(in_8), .B1(in_17), .A2(in_7), .B2(in_16), .A3(in_6), .B3(in_15), .A4(in_5),
    .B4(in_14), .A5(in_4), .B5(in_13), .A6(in_3), .B6(in_12), .A7(in_2), .B7(in_11), .S0(out_40),
    .S1(out_39), .S2(out_38), .S3(out_37), .S4(out_36), .S5(out_35), .S6(out_34), .S7(out_33), .C(overflow),
    .C0(mantissa_1_out_13));
  mantissa mantissa_1 (
    .in_1(in_24), .in_2(in_23), .in_9(in_22), .in_10(in_21), .in_11(in_20), .in_12(in_19), .in_3(in_25),
    .in_4(in_26), .in_5(in_27), .in_6(in_28), .in_7(in_29), .in_8(in_30), .out_13(mantissa_1_out_13),
    .out_15(out_41), .out_16(out_42), .out_17(out_43), .out_18(out_44), .out_19(out_45), .out_20(out_46),
    .out_21(out_47), .out_22(out_48), .out_23(out_49), .out_24(out_50), .out_25(out_51), .out_26(out_52));  // open: out_14
endmodule

module sign (
  input  in_1,
  input  in_2,
  output out_3
);

  xor xor_1 (out_3, in_1, in_2);
endmodule

module mantissa (
  input  in_1,
  input  in_2,
  input  in_3,
  input  in_4,
  input  in_5,
  input  in_6,
  input  in_7,
  input  in_8,
  input  in_9,
  input  in_10,
  input  in_11,
  input  in_12,
  output out_13,
  output out_14,
  output out_15,
  output out_16,
  output out_17,
  output out_18,
  output out_19,
  output out_20,
  output out_21,
  output out_22,
  output out_23,
  output out_24,
  output out_25,
  output out_26
);

  wire and_1_out, and_2_out, and_3_out, and_4_out, and_5_out, and_6_out, and_7_out, and_8_out, and_9_out,
       and_10_out, and_11_out, and_12_out, and_13_out, and_14_out, and_15_out, and_16_out, and_17_out,
       and_18_out, and_19_out, and_20_out, and_21_out, and_22_out, and_23_out, and_24_out, and_25_out,
       and_26_out, and_27_out, and_28_out, and_29_out, and_30_out, and_31_out, and_32_out, and_33_out,
       and_34_out, and_35_out, and_36_out, and_37_out, and_38_out, and_39_out, and_40_out, and_41_out,
       and_42_out, and_43_out, and_44_out, and_45_out, and_46_out, and_47_out, and_48_out, n7_adder_2_out_16,
       n7_adder_2_out_17, n7_adder_2_out_18, n7_adder_2_out_19, n7_adder_2_out_20, n7_adder_2_out_21,
       n7_adder_2_out_22, n7_adder_3_out_16, n7_adder_3_out_17, n7_adder_3_out_18, n7_adder_3_out_19,
       n7_adder_3_out_20, n7_adder_3_out_21, n7_adder_3_out_22, n7_adder_4_out_16, n7_adder_4_out_17,
       n7_adder_4_out_18, n7_adder_4_out_19, n7_adder_4_out_20, n7_adder_4_out_21, n7_adder_4_out_22,
       n7_adder_5_out_16, n7_adder_5_out_17, n7_adder_5_out_18, n7_adder_5_out_19, n7_adder_5_out_20,
       n7_adder_5_out_21, n7_adder_5_out_22, n7_adder_6_out_16, n7_adder_6_out_17, n7_adder_6_out_18,
       n7_adder_6_out_19, n7_adder_6_out_20, n7_adder_6_out_21, n7_adder_6_out_22, not_1_out;

  and and_1 (and_1_out, in_3, 1'b1);
  and and_2 (and_2_out, 1'b1, 1'b1);
  and and_3 (and_3_out, in_4, 1'b1);
  and and_4 (and_4_out, 1'b1, in_12);
  and and_5 (and_5_out, in_5, 1'b1);
  and and_6 (and_6_out, in_3, in_12);
  and and_7 (and_7_out, in_4, in_12);
  and and_8 (and_8_out, in_7, 1'b1);
  and and_9 (and_9_out, in_6, 1'b1);
  and and_10 (and_10_out, 1'b1, in_11);
  and and_11 (and_11_out, in_5, in_12);
  and and_12 (and_12_out, in_8, 1'b1);
  and and_13 (and_13_out, in_4, in_11);
  and and_14 (and_14_out, in_3, in_11);
  and and_15 (and_15_out, in_6, in_12);
  and and_16 (and_16_out, 1'b1, in_10);
  and and_17 (and_17_out, in_5, in_11);
  and and_18 (and_18_out, in_7, in_12);
  and and_19 (and_19_out, in_8, in_12);
  _7_adder u_7_adder_1 (
    .in_1(n7_adder_2_out_16), .in_2(and_12_out), .in_3(n7_adder_2_out_17), .in_4(and_8_out),
    .in_5(n7_adder_2_out_18), .in_6(and_9_out), .in_7(n7_adder_2_out_19), .in_8(and_5_out),
    .in_9(n7_adder_2_out_20), .in_10(and_3_out), .in_11(n7_adder_2_out_21), .in_12(and_1_out),
    .in_13(n7_adder_2_out_22), .in_14(and_2_out), .out_15(out_20), .out_16(out_19), .out_17(out_18),
    .out_18(out_17), .out_19(out_16), .out_20(out_15), .out_21(out_14), .out_22(out_13));
  and and_20 (and_20_out, in_3, in_10);
  and and_21 (and_21_out, in_6, in_11);
  and and_22 (and_22_out, 1'b1, in_9);
  and and_23 (and_23_out, in_5, in_10);
  and and_24 (and_24_out, in_4, in_10);
  and and_25 (and_25_out, in_8, in_11);
  and and_26 (and_26_out, in_7, in_11);
  _7_adder u_7_adder_2 (
    .in_1(n7_adder_3_out_16), .in_2(and_19_out), .in_3(n7_adder_3_out_17), .in_4(and_18_out),
    .in_5(n7_adder_3_out_18), .in_6(and_15_out), .in_7(n7_adder_3_out_19), .in_8(and_11_out),
    .in_9(n7_adder_3_out_20), .in_10(and_7_out), .in_11(n7_adder_3_out_21), .in_12(and_6_out),
    .in_13(n7_adder_3_out_22), .in_14(and_4_out), .out_15(out_21), .out_16(n7_adder_2_out_16),
    .out_17(n7_adder_2_out_17), .out_18(n7_adder_2_out_18), .out_19(n7_adder_2_out_19),
    .out_20(n7_adder_2_out_20), .out_21(n7_adder_2_out_21), .out_22(n7_adder_2_out_22));
  and and_27 (and_27_out, in_3, in_9);
  and and_28 (and_28_out, in_6, in_10);
  and and_29 (and_29_out, 1'b1, in_2);
  and and_30 (and_30_out, in_4, in_9);
  and and_31 (and_31_out, in_5, in_9);
  and and_32 (and_32_out, in_7, in_10);
  _7_adder u_7_adder_3 (
    .in_1(n7_adder_4_out_16), .in_2(and_25_out), .in_3(n7_adder_4_out_17), .in_4(and_26_out),
    .in_5(n7_adder_4_out_18), .in_6(and_21_out), .in_7(n7_adder_4_out_19), .in_8(and_17_out),
    .in_9(n7_adder_4_out_20), .in_10(and_13_out), .in_11(n7_adder_4_out_21), .in_12(and_14_out),
    .in_13(n7_adder_4_out_22), .in_14(and_10_out), .out_15(out_22), .out_16(n7_adder_3_out_16),
    .out_17(n7_adder_3_out_17), .out_18(n7_adder_3_out_18), .out_19(n7_adder_3_out_19),
    .out_20(n7_adder_3_out_20), .out_21(n7_adder_3_out_21), .out_22(n7_adder_3_out_22));
  and and_33 (and_33_out, in_3, in_2);
  and and_34 (and_34_out, in_6, in_9);
  and and_35 (and_35_out, in_8, in_10);
  and and_36 (and_36_out, in_4, in_2);
  and and_37 (and_37_out, in_7, in_9);
  _7_adder u_7_adder_4 (
    .in_1(n7_adder_5_out_16), .in_2(and_35_out), .in_3(n7_adder_5_out_17), .in_4(and_32_out),
    .in_5(n7_adder_5_out_18), .in_6(and_28_out), .in_7(n7_adder_5_out_19), .in_8(and_23_out),
    .in_9(n7_adder_5_out_20), .in_10(and_24_out), .in_11(n7_adder_5_out_21), .in_12(and_20_out),
    .in_13(n7_adder_5_out_22), .in_14(and_16_out), .out_15(out_23), .out_16(n7_adder_4_out_16),
    .out_17(n7_adder_4_out_17), .out_18(n7_adder_4_out_18), .out_19(n7_adder_4_out_19),
    .out_20(n7_adder_4_out_20), .out_21(n7_adder_4_out_21), .out_22(n7_adder_4_out_22));
  and and_38 (and_38_out, in_6, in_2);
  and and_39 (and_39_out, in_5, in_2);
  and and_40 (and_40_out, in_8, in_9);
  and and_41 (and_41_out, in_7, in_2);
  and and_42 (and_42_out, in_8, in_2);
  _7_adder u_7_adder_5 (
    .in_1(n7_adder_6_out_16), .in_2(and_40_out), .in_3(n7_adder_6_out_17), .in_4(and_37_out),
    .in_5(n7_adder_6_out_18), .in_6(and_34_out), .in_7(n7_adder_6_out_19), .in_8(and_31_out),
    .in_9(n7_adder_6_out_20), .in_10(and_30_out), .in_11(n7_adder_6_out_21), .in_12(and_27_out),
    .in_13(n7_adder_6_out_22), .in_14(and_22_out), .out_15(out_24), .out_16(n7_adder_5_out_16),
    .out_17(n7_adder_5_out_17), .out_18(n7_adder_5_out_18), .out_19(n7_adder_5_out_19),
    .out_20(n7_adder_5_out_20), .out_21(n7_adder_5_out_21), .out_22(n7_adder_5_out_22));
  and and_43 (and_43_out, 1'b1, in_1);
  not not_1 (not_1_out, 1'b1);
  and and_44 (and_44_out, in_3, in_1);
  _7_adder u_7_adder_6 (
    .in_1(and_48_out), .in_2(and_42_out), .in_3(and_47_out), .in_4(and_41_out), .in_5(and_45_out),
    .in_6(and_38_out), .in_7(and_46_out), .in_8(and_39_out), .in_9(and_44_out), .in_10(and_36_out),
    .in_11(and_43_out), .in_12(and_33_out), .in_13(not_1_out), .in_14(and_29_out), .out_15(out_25),
    .out_16(n7_adder_6_out_16), .out_17(n7_adder_6_out_17), .out_18(n7_adder_6_out_18),
    .out_19(n7_adder_6_out_19), .out_20(n7_adder_6_out_20), .out_21(n7_adder_6_out_21),
    .out_22(n7_adder_6_out_22));
  and and_45 (and_45_out, in_5, in_1);
  and and_46 (and_46_out, in_4, in_1);
  and and_47 (and_47_out, in_6, in_1);
  and and_48 (and_48_out, in_7, in_1);
  and and_49 (out_26, in_8, in_1);
endmodule

module mantissa2 (
  input  in_1,
  input  in_2,
  input  in_3,
  input  in_4,
  input  in_5,
  input  in_6,
  input  in_7,
  input  in_8,
  input  in_9,
  input  in_10,
  input  in_11,
  input  in_12,
  output out_13,
  output out_14,
  output out_15,
  output out_16,
  output out_17,
  output out_18,
  output out_19,
  output out_20,
  output out_21,
  output out_22,
  output out_23,
  output out_24,
  output out_25,
  output out_26,
  output out_27,
  output out_28
);

  wire and_1_out, and_2_out, and_3_out, and_4_out, and_5_out, and_6_out, and_7_out, and_8_out, and_9_out,
       and_10_out, and_11_out, and_12_out, and_13_out, and_14_out, and_15_out, and_16_out, and_17_out,
       and_18_out, and_19_out, and_20_out, and_21_out, and_22_out, and_23_out, and_24_out, and_25_out,
       and_26_out, and_27_out, and_28_out, and_29_out, and_30_out, and_31_out, and_32_out, and_33_out,
       and_34_out, and_35_out, half_adder_1_c, half_adder_1_s, half_adder_2_c, half_adder_2_s,
       half_adder_3_c, half_adder_3_s, n2_adder_1_out_5, n2_adder_1_out_6, n2_adder_1_out_7,
       n2_adder_2_out_5, n2_adder_2_out_6, n2_adder_2_out_7, n6_adder_2_out_14, n6_adder_2_out_15,
       n6_adder_2_out_16, n6_adder_2_out_17, n6_adder_2_out_18, n6_adder_2_out_19, n6_adder_3_out_14,
       n6_adder_3_out_15, n6_adder_3_out_16, n6_adder_3_out_17, n6_adder_3_out_18, n6_adder_3_out_19,
       n6_adder_4_out_14, n6_adder_4_out_15, n6_adder_4_out_16, n6_adder_4_out_17, n6_adder_4_out_18,
       n6_adder_4_out_19, n6_adder_5_out_14, n6_adder_5_out_15, n6_adder_5_out_16, n6_adder_5_out_17,
       n6_adder_5_out_18, n6_adder_5_out_19, not_1_out, not_2_out;

  and and_1 (and_1_out, in_3, in_12);
  and and_2 (and_2_out, in_4, in_12);
  and and_3 (and_3_out, in_5, in_12);
  and and_4 (and_4_out, in_3, in_11);
  and and_5 (and_5_out, in_6, in_12);
  not not_1 (not_1_out, 1'b1);
  and and_6 (and_6_out, in_5, in_11);
  and and_7 (and_7_out, in_4, in_11);
  and and_8 (and_8_out, in_7, in_12);
  Half_Adder half_adder_1 (.B(out_15), .A(out_14), .S(half_adder_1_s), .C(half_adder_1_c));
  _2_adder u_2_adder_1 (
    .in_1(half_adder_1_s), .in_2(out_13), .in_3(half_adder_1_c), .in_4(not_1_out), .out_5(n2_adder_1_out_5),
    .out_6(n2_adder_1_out_6), .out_7(n2_adder_1_out_7));
  and and_9 (and_9_out, in_3, in_10);
  and and_10 (and_10_out, in_6, in_11);
  and and_11 (and_11_out, in_8, in_12);
  Half_Adder half_adder_2 (.B(out_17), .A(out_16), .S(half_adder_2_s), .C(half_adder_2_c));
  _3_adder u_3_adder_1 (
    .in_1(n2_adder_2_out_5), .in_2(n2_adder_1_out_5), .in_3(n2_adder_2_out_6), .in_4(n2_adder_1_out_6),
    .in_5(n2_adder_2_out_7), .in_6(n2_adder_1_out_7), .out_7(out_28), .out_8(out_27), .out_9(out_26),
    .out_10(out_25));
  and and_12 (and_12_out, in_5, in_10);
  and and_13 (and_13_out, in_4, in_10);
  and and_14 (and_14_out, in_7, in_11);
  _6_adder u_6_adder_1 (
    .in_1(n6_adder_2_out_14), .in_2(n6_adder_2_out_15), .in_3(and_11_out), .in_4(and_8_out),
    .in_5(n6_adder_2_out_16), .in_6(and_5_out), .in_7(n6_adder_2_out_17), .in_8(and_3_out),
    .in_9(n6_adder_2_out_18), .in_10(and_2_out), .in_11(n6_adder_2_out_19), .in_12(and_1_out),
    .out_13(out_19), .out_14(out_18), .out_15(out_17), .out_16(out_16), .out_17(out_15), .out_18(out_14),
    .out_19(out_13));
  Half_Adder half_adder_3 (.B(out_19), .A(out_18), .S(half_adder_3_s), .C(half_adder_3_c));
  _2_adder u_2_adder_2 (
    .in_1(half_adder_3_s), .in_2(half_adder_2_s), .in_3(half_adder_3_c), .in_4(half_adder_2_c),
    .out_5(n2_adder_2_out_5), .out_6(n2_adder_2_out_6), .out_7(n2_adder_2_out_7));
  and and_15 (and_15_out, in_3, in_9);
  and and_16 (and_16_out, in_6, in_10);
  and and_17 (and_17_out, in_8, in_11);
  and and_18 (and_18_out, in_5, in_9);
  and and_19 (and_19_out, in_4, in_9);
  and and_20 (and_20_out, in_7, in_10);
  _6_adder u_6_adder_2 (
    .in_1(n6_adder_3_out_14), .in_2(n6_adder_3_out_15), .in_3(and_17_out), .in_4(and_14_out),
    .in_5(n6_adder_3_out_16), .in_6(and_10_out), .in_7(n6_adder_3_out_17), .in_8(and_6_out),
    .in_9(n6_adder_3_out_18), .in_10(and_7_out), .in_11(n6_adder_3_out_19), .in_12(and_4_out),
    .out_13(out_20), .out_14(n6_adder_2_out_14), .out_15(n6_adder_2_out_15), .out_16(n6_adder_2_out_16),
    .out_17(n6_adder_2_out_17), .out_18(n6_adder_2_out_18), .out_19(n6_adder_2_out_19));
  and and_21 (and_21_out, in_3, in_1);
  and and_22 (and_22_out, in_6, in_9);
  and and_23 (and_23_out, in_8, in_10);
  and and_24 (and_24_out, in_4, in_1);
  and and_25 (and_25_out, in_5, in_1);
  and and_26 (and_26_out, in_7, in_9);
  _6_adder u_6_adder_3 (
    .in_1(n6_adder_4_out_14), .in_2(n6_adder_4_out_15), .in_3(and_23_out), .in_4(and_20_out),
    .in_5(n6_adder_4_out_16), .in_6(and_16_out), .in_7(n6_adder_4_out_17), .in_8(and_12_out),
    .in_9(n6_adder_4_out_18), .in_10(and_13_out), .in_11(n6_adder_4_out_19), .in_12(and_9_out),
    .out_13(out_21), .out_14(n6_adder_3_out_14), .out_15(n6_adder_3_out_15), .out_16(n6_adder_3_out_16),
    .out_17(n6_adder_3_out_17), .out_18(n6_adder_3_out_18), .out_19(n6_adder_3_out_19));
  and and_27 (and_27_out, in_6, in_1);
  and and_28 (and_28_out, in_8, in_9);
  and and_29 (and_29_out, in_7, in_1);
  _6_adder u_6_adder_4 (
    .in_1(n6_adder_5_out_14), .in_2(n6_adder_5_out_15), .in_3(and_28_out), .in_4(and_26_out),
    .in_5(n6_adder_5_out_16), .in_6(and_22_out), .in_7(n6_adder_5_out_17), .in_8(and_18_out),
    .in_9(n6_adder_5_out_18), .in_10(and_19_out), .in_11(n6_adder_5_out_19), .in_12(and_15_out),
    .out_13(out_22), .out_14(n6_adder_4_out_14), .out_15(n6_adder_4_out_15), .out_16(n6_adder_4_out_16),
    .out_17(n6_adder_4_out_17), .out_18(n6_adder_4_out_18), .out_19(n6_adder_4_out_19));
  and and_30 (and_30_out, in_8, in_1);
  not not_2 (not_2_out, 1'b1);
  and and_31 (and_31_out, in_3, in_2);
  _6_adder u_6_adder_5 (
    .in_1(and_35_out), .in_2(and_34_out), .in_3(and_30_out), .in_4(and_29_out), .in_5(and_33_out),
    .in_6(and_27_out), .in_7(and_32_out), .in_8(and_25_out), .in_9(and_31_out), .in_10(and_24_out),
    .in_11(not_2_out), .in_12(and_21_out), .out_13(out_23), .out_14(n6_adder_5_out_14),
    .out_15(n6_adder_5_out_15), .out_16(n6_adder_5_out_16), .out_17(n6_adder_5_out_17),
    .out_18(n6_adder_5_out_18), .out_19(n6_adder_5_out_19));
  and and_32 (and_32_out, in_4, in_2);
  and and_33 (and_33_out, in_5, in_2);
  and and_34 (and_34_out, in_6, in_2);
  and and_35 (and_35_out, in_7, in_2);
  and and_36 (out_24, in_8, in_2);
endmodule

module exponent (
  input  C0,
  input  A0,
  input  B0,
  input  A1,
  input  B1,
  input  A2,
  input  B2,
  input  A3,
  input  B3,
  input  A4,
  input  B4,
  input  A5,
  input  B5,
  input  A6,
  input  B6,
  input  A7,
  input  B7,
  output S0,
  output S1,
  output S2,
  output S3,
  output S4,
  output S5,
  output S6,
  output S7,
  output C
);

  wire full_adder_1_c_2, full_adder_2_c_2, full_adder_3_c_2, full_adder_4_c_2, full_adder_5_c_2,
       full_adder_6_c_2, full_adder_7_c_2;

  Full_Adder full_adder_1 (.B(A0), .A(B0), .C(C0), .S(S0), .C_2(full_adder_1_c_2));
  Full_Adder full_adder_2 (.B(A1), .A(B1), .C(full_adder_1_c_2), .S(S1), .C_2(full_adder_2_c_2));
  Full_Adder full_adder_3 (.B(A2), .A(B2), .C(full_adder_2_c_2), .S(S2), .C_2(full_adder_3_c_2));
  Full_Adder full_adder_4 (.B(A3), .A(B3), .C(full_adder_3_c_2), .S(S3), .C_2(full_adder_4_c_2));
  Full_Adder full_adder_5 (.B(A4), .A(B4), .C(full_adder_4_c_2), .S(S4), .C_2(full_adder_5_c_2));
  Full_Adder full_adder_6 (.B(A5), .A(B5), .C(full_adder_5_c_2), .S(S5), .C_2(full_adder_6_c_2));
  Full_Adder full_adder_7 (.B(A6), .A(B6), .C(full_adder_6_c_2), .S(S6), .C_2(full_adder_7_c_2));
  Full_Adder full_adder_8 (.B(A7), .A(B7), .C(full_adder_7_c_2), .S(S7), .C_2(C));
endmodule

module Half_Adder (
  input  B,
  input  A,
  output S,
  output C
);

  xor xor_1 (S, B, A);
  and and_1 (C, B, A);
endmodule

module Full_Adder (
  input  B,
  input  A,
  input  C,
  output S,
  output C_2
);

  wire and_1_out, and_2_out, xor_1_out;

  xor xor_1 (xor_1_out, B, A);
  and and_1 (and_1_out, xor_1_out, C);
  and and_2 (and_2_out, B, A);
  xor xor_2 (S, xor_1_out, C);
  or or_1 (C_2, and_1_out, and_2_out);

  // Notes on the sheet:
  //   P
  //   G
  //   PC
endmodule

module _2_adder (
  input  in_1,
  input  in_2,
  input  in_3,
  input  in_4,
  output out_5,
  output out_6,
  output out_7
);

  wire half_adder_1_c;

  Half_Adder half_adder_1 (.B(in_1), .A(in_2), .S(out_5), .C(half_adder_1_c));
  Full_Adder full_adder_1 (.B(in_3), .A(in_4), .C(half_adder_1_c), .S(out_6), .C_2(out_7));
endmodule

module _3_adder (
  input  in_1,
  input  in_2,
  input  in_3,
  input  in_4,
  input  in_5,
  input  in_6,
  output out_7,
  output out_8,
  output out_9,
  output out_10
);

  wire full_adder_1_c_2, half_adder_1_c;

  Half_Adder half_adder_1 (.B(in_1), .A(in_2), .S(out_7), .C(half_adder_1_c));
  Full_Adder full_adder_1 (.B(in_3), .A(in_4), .C(half_adder_1_c), .S(out_8), .C_2(full_adder_1_c_2));
  Full_Adder full_adder_2 (.B(in_5), .A(in_6), .C(full_adder_1_c_2), .S(out_9), .C_2(out_10));
endmodule

module _6_adder (
  input  in_1,
  input  in_2,
  input  in_3,
  input  in_4,
  input  in_5,
  input  in_6,
  input  in_7,
  input  in_8,
  input  in_9,
  input  in_10,
  input  in_11,
  input  in_12,
  output out_13,
  output out_14,
  output out_15,
  output out_16,
  output out_17,
  output out_18,
  output out_19
);

  wire and_1_out, and_2_out, and_3_out, and_4_out, and_5_out, and_6_out, and_7_out, and_8_out, and_9_out,
       and_10_out, and_11_out, or_1_out, or_2_out, or_3_out, or_4_out, xor_2_out, xor_4_out, xor_6_out,
       xor_8_out, xor_10_out;

  xor xor_1 (out_13, in_1, in_3);
  xor xor_2 (xor_2_out, in_7, in_8);
  and and_1 (and_1_out, in_1, in_3);
  and and_2 (and_2_out, xor_2_out, or_4_out);
  and and_3 (and_3_out, in_7, in_8);
  xor xor_3 (out_16, xor_2_out, or_4_out);
  xor xor_4 (xor_4_out, in_2, in_4);
  and and_4 (and_4_out, in_2, in_4);
  or or_1 (or_1_out, and_2_out, and_3_out);
  and and_5 (and_5_out, xor_4_out, and_1_out);
  xor xor_5 (out_14, xor_4_out, and_1_out);
  xor xor_6 (xor_6_out, in_9, in_10);
  and and_6 (and_6_out, in_9, in_10);
  or or_2 (or_2_out, and_5_out, and_4_out);
  xor xor_7 (out_17, xor_6_out, or_1_out);
  and and_7 (and_7_out, xor_6_out, or_1_out);
  or or_3 (or_3_out, and_7_out, and_6_out);
  xor xor_8 (xor_8_out, in_5, in_6);
  and and_8 (and_8_out, in_5, in_6);
  xor xor_9 (out_15, xor_8_out, or_2_out);
  and and_9 (and_9_out, xor_8_out, or_2_out);
  xor xor_10 (xor_10_out, in_11, in_12);
  or or_4 (or_4_out, and_9_out, and_8_out);
  and and_10 (and_10_out, xor_10_out, or_3_out);
  and and_11 (and_11_out, in_11, in_12);
  xor xor_11 (out_18, xor_10_out, or_3_out);
  or or_5 (out_19, and_10_out, and_11_out);
endmodule

module _7_adder (
  input  in_1,
  input  in_2,
  input  in_3,
  input  in_4,
  input  in_5,
  input  in_6,
  input  in_7,
  input  in_8,
  input  in_9,
  input  in_10,
  input  in_11,
  input  in_12,
  input  in_13,
  input  in_14,
  output out_15,
  output out_16,
  output out_17,
  output out_18,
  output out_19,
  output out_20,
  output out_21,
  output out_22
);

  wire full_adder_1_c_2, full_adder_2_c_2, full_adder_3_c_2, full_adder_4_c_2, full_adder_5_c_2,
       half_adder_1_c;

  Half_Adder half_adder_1 (.B(in_1), .A(in_2), .S(out_15), .C(half_adder_1_c));
  Full_Adder full_adder_1 (.B(in_3), .A(in_4), .C(half_adder_1_c), .S(out_16), .C_2(full_adder_1_c_2));
  Full_Adder full_adder_2 (.B(in_5), .A(in_6), .C(full_adder_1_c_2), .S(out_17), .C_2(full_adder_2_c_2));
  Full_Adder full_adder_3 (.B(in_7), .A(in_8), .C(full_adder_2_c_2), .S(out_18), .C_2(full_adder_3_c_2));
  Full_Adder full_adder_4 (.B(in_9), .A(in_10), .C(full_adder_3_c_2), .S(out_19), .C_2(full_adder_4_c_2));
  Full_Adder full_adder_5 (.B(in_11), .A(in_12), .C(full_adder_4_c_2), .S(out_20), .C_2(full_adder_5_c_2));
  Full_Adder full_adder_6 (.B(in_13), .A(in_14), .C(full_adder_5_c_2), .S(out_21), .C_2(out_22));
endmodule
