// Logisim project csproject.circ as structural Verilog: 12 circuits, main circuit main
module main (
  input  A,
  input  in_2,
  input  in_3,
  input  in_4,
  input  in_5,
  input  in_6,
  input  in_7,
  input  in_8,
  input  in_9,
  input  in_10,
  input  in_11,
  input  in_12,
  input  in_13,
  input  in_14,
  input  in_15,
  input  B,
  input  in_17,
  input  in_18,
  input  in_19,
  input  in_20,
  input  in_21,
  input  in_22,
  input  in_23,
  input  in_24,
  input  in_25,
  input  in_26,
  input  in_27,
  input  in_28,
  input  in_29,
  input  in_30,
  input  in_31,
  output out_32,
  output out_33,
  output out_34,
  output out_35,
  output out_36,
  output out_37,
  output out_38,
  output out_39,
  output out_40,
  output out_41,
  output out_42,
  output out_43,
  output overflow,
  output out_45,
  output out_46,
  output out_47,
  output out_48,
  output out_49,
  output out_50,
  output out_51,
  output out_52,
  output out_53
);

  wire clock_1_out, mantissa_1_out_13, mantissa_1_out_14, mantissa_1_out_15, mantissa_1_out_16,
       mantissa_1_out_17, mantissa_1_out_18, mantissa_1_out_19, mantissa_1_out_20, mantissa_1_out_21,
       mantissa_1_out_22, mantissa_1_out_23, mantissa_1_out_24, mantissa_1_out_25, mantissa_1_out_26;

  sign sign_1 (.in_1(A), .in_2(B), .out_3(out_45));
  exponent exponent_1 (
    .A0(in_9), .B0(in_24), .A1(in_8), .B1(in_23), .A2(in_7), .B2(in_22), .A3(in_6), .B3(in_21), .A4(in_5),
    .B4(in_20), .A5(in_4), .B5(in_19), .A6(in_3), .B6(in_18), .A7(in_2), .B7(in_17), .S0(out_53),
    .S1(out_52), .S2(out_51), .S3(out_50), .S4(out_49), .S5(out_48), .S6(out_47), .S7(out_46), .C(overflow),
    .C0(mantissa_1_out_13));
  shift shift_1 (
    .out_17(out_32), .out_18(out_33), .out_19(out_34), .out_20(out_35), .out_21(out_36), .out_22(out_37),
    .out_23(out_38), .out_24(out_39), .out_25(out_40), .out_26(out_41), .out_27(out_42), .Reset(in_31),
    ._11(mantissa_1_out_15), ._10(mantissa_1_out_16), ._9(mantissa_1_out_17), ._8(mantissa_1_out_18),
    ._7(mantissa_1_out_19), ._6(mantissa_1_out_20), ._5(mantissa_1_out_21), ._4(mantissa_1_out_22),
    ._3(mantissa_1_out_23), ._2(mantissa_1_out_24), ._1(mantissa_1_out_25), ._0(mantissa_1_out_26),
    .in_15(mantissa_1_out_13), .out_28(out_43), ._12(mantissa_1_out_14), .Clock(clock_1_out));
  mantissa mantissa_1 (
    .in_1(in_15), .in_2(in_14), .in_9(in_13), .in_10(in_12), .in_11(in_11), .in_12(in_10), .in_3(in_25),
    .in_4(in_26), .in_5(in_27), .in_6(in_28), .in_7(in_29), .in_8(in_30), .out_13(mantissa_1_out_13),
    .out_14(mantissa_1_out_14), .out_15(mantissa_1_out_15), .out_16(mantissa_1_out_16),
    .out_17(mantissa_1_out_17), .out_18(mantissa_1_out_18), .out_19(mantissa_1_out_19),
    .out_20(mantissa_1_out_20), .out_21(mantissa_1_out_21), .out_22(mantissa_1_out_22),
    .out_23(mantissa_1_out_23), .out_24(mantissa_1_out_24), .out_25(mantissa_1_out_25),
    .out_26(mantissa_1_out_26));
  Clock clock_1 (.out(clock_1_out));

  // Notes on the sheet:
  //   Clock
  //   Reset (遊戲中當Start)
endmodule

module sign (
  input  in_1,
  input  in_2,
  output out_3
);

  xor xor_1 (out_3, in_1, in_2);
endmodule

module mantissa (
  input  in_1,
  input  in_2,
  input  in_3,
  input  in_4,
  input  in_5,
  input  in_6,
  input  in_7,
  input  in_8,
  input  in_9,
  input  in_10,
  input  in_11,
  input  in_12,
  output out_13,
  output out_14,
  output out_15,
  output out_16,
  output out_17,
  output out_18,
  output out_19,
  output out_20,
  output out_21,
  output out_22,
  output out_23,
  output out_24,
  output out_25,
  output out_26
);

  wire and_1_out, and_2_out, and_3_out, and_4_out, and_5_out, and_6_out, and_7_out, and_8_out, and_9_out,
       and_10_out, and_11_out, and_12_out, and_13_out, and_14_out, and_15_out, and_16_out, and_17_out,
       and_18_out, and_19_out, and_20_out, and_21_out, and_22_out, and_23_out, and_24_out, and_25_out,
       and_26_out, and_27_out, and_28_out, and_29_out, and_30_out, and_31_out, and_32_out, and_33_out,
       and_34_out, and_35_out, and_36_out, and_37_out, and_38_out, and_39_out, and_40_out, and_41_out,
       and_42_out, and_43_out, and_44_out, and_45_out, and_46_out, and_47_out, and_48_out, n7_adder_2_out_16,
       n7_adder_2_out_17, n7_adder_2_out_18, n7_adder_2_out_19, n7_adder_2_out_20, n7_adder_2_out_21,
       n7_adder_2_out_22, n7_adder_3_out_16, n7_adder_3_out_17, n7_adder_3_out_18, n7_adder_3_out_19,
       n7_adder_3_out_20, n7_adder_3_out_21, n7_adder_3_out_22, n7_adder_4_out_16, n7_adder_4_out_17,
       n7_adder_4_out_18, n7_adder_4_out_19, n7_adder_4_out_20, n7_adder_4_out_21, n7_adder_4_out_22,
       n7_adder_5_out_16, n7_adder_5_out_17, n7_adder_5_out_18, n7_adder_5_out_19, n7_adder_5_out_20,
       n7_adder_5_out_21, n7_adder_5_out_22, n7_adder_6_out_16, n7_adder_6_out_17, n7_adder_6_out_18,
       n7_adder_6_out_19, n7_adder_6_out_20, n7_adder_6_out_21, n7_adder_6_out_22, not_1_out;

  and and_1 (and_1_out, 1'b1, 1'b1);
  and and_2 (and_2_out, in_3, 1'b1);
  and and_3 (and_3_out, in_4, 1'b1);
  and and_4 (and_4_out, 1'b1, in_12);
  and and_5 (and_5_out, in_5, 1'b1);
  and and_6 (and_6_out, in_3, in_12);
  and and_7 (and_7_out, in_4, in_12);
  and and_8 (and_8_out, in_7, 1'b1);
  and and_9 (and_9_out, in_6, 1'b1);
  and and_10 (and_10_out, 1'b1, in_11);
  and and_11 (and_11_out, in_5, in_12);
  and and_12 (and_12_out, in_8, 1'b1);
  and and_13 (and_13_out, in_3, in_11);
  and and_14 (and_14_out, in_4, in_11);
  and and_15 (and_15_out, in_6, in_12);
  and and_16 (and_16_out, 1'b1, in_10);
  and and_17 (and_17_out, in_5, in_11);
  and and_18 (and_18_out, in_7, in_12);
  and and_19 (and_19_out, in_8, in_12);
  _7_adder u_7_adder_1 (
    .in_1(n7_adder_2_out_16), .in_2(and_12_out), .in_3(n7_adder_2_out_17), .in_4(and_8_out),
    .in_5(n7_adder_2_out_18), .in_6(and_9_out), .in_7(n7_adder_2_out_19), .in_8(and_5_out),
    .in_9(n7_adder_2_out_20), .in_10(and_3_out), .in_11(n7_adder_2_out_21), .in_12(and_2_out),
    .in_13(n7_adder_2_out_22), .in_14(and_1_out), .out_15(out_20), .out_16(out_19), .out_17(out_18),
    .out_18(out_17), .out_19(out_16), .out_20(out_15), .out_21(out_14), .out_22(out_13));
  and and_20 (and_20_out, in_3, in_10);
  and and_21 (and_21_out, in_6, in_11);
  and and_22 (and_22_out, 1'b1, in_9);
  and and_23 (and_23_out, in_4, in_10);
  and and_24 (and_24_out, in_5, in_10);
  and and_25 (and_25_out, in_7, in_11);
  and and_26 (and_26_out, in_8, in_11);
  _7_adder u_7_adder_2 (
    .in_1(n7_adder_3_out_16), .in_2(and_19_out), .in_3(n7_adder_3_out_17), .in_4(and_18_out),
    .in_5(n7_adder_3_out_18), .in_6(and_15_out), .in_7(n7_adder_3_out_19), .in_8(and_11_out),
    .in_9(n7_adder_3_out_20), .in_10(and_7_out), .in_11(n7_adder_3_out_21), .in_12(and_6_out),
    .in_13(n7_adder_3_out_22), .in_14(and_4_out), .out_15(out_21), .out_16(n7_adder_2_out_16),
    .out_17(n7_adder_2_out_17), .out_18(n7_adder_2_out_18), .out_19(n7_adder_2_out_19),
    .out_20(n7_adder_2_out_20), .out_21(n7_adder_2_out_21), .out_22(n7_adder_2_out_22));
  and and_27 (and_27_out, in_3, in_9);
  and and_28 (and_28_out, in_6, in_10);
  and and_29 (and_29_out, 1'b1, in_2);
  and and_30 (and_30_out, in_4, in_9);
  and and_31 (and_31_out, in_5, in_9);
  and and_32 (and_32_out, in_7, in_10);
  _7_adder u_7_adder_3 (
    .in_1(n7_adder_4_out_16), .in_2(and_26_out), .in_3(n7_adder_4_out_17), .in_4(and_25_out),
    .in_5(n7_adder_4_out_18), .in_6(and_21_out), .in_7(n7_adder_4_out_19), .in_8(and_17_out),
    .in_9(n7_adder_4_out_20), .in_10(and_14_out), .in_11(n7_adder_4_out_21), .in_12(and_13_out),
    .in_13(n7_adder_4_out_22), .in_14(and_10_out), .out_15(out_22), .out_16(n7_adder_3_out_16),
    .out_17(n7_adder_3_out_17), .out_18(n7_adder_3_out_18), .out_19(n7_adder_3_out_19),
    .out_20(n7_adder_3_out_20), .out_21(n7_adder_3_out_21), .out_22(n7_adder_3_out_22));
  and and_33 (and_33_out, in_3, in_2);
  and and_34 (and_34_out, in_6, in_9);
  and and_35 (and_35_out, in_8, in_10);
  and and_36 (and_36_out, in_4, in_2);
  and and_37 (and_37_out, in_7, in_9);
  _7_adder u_7_adder_4 (
    .in_1(n7_adder_5_out_16), .in_2(and_35_out), .in_3(n7_adder_5_out_17), .in_4(and_32_out),
    .in_5(n7_adder_5_out_18), .in_6(and_28_out), .in_7(n7_adder_5_out_19), .in_8(and_24_out),
    .in_9(n7_adder_5_out_20), .in_10(and_23_out), .in_11(n7_adder_5_out_21), .in_12(and_20_out),
    .in_13(n7_adder_5_out_22), .in_14(and_16_out), .out_15(out_23), .out_16(n7_adder_4_out_16),
    .out_17(n7_adder_4_out_17), .out_18(n7_adder_4_out_18), .out_19(n7_adder_4_out_19),
    .out_20(n7_adder_4_out_20), .out_21(n7_adder_4_out_21), .out_22(n7_adder_4_out_22));
  and and_38 (and_38_out, in_5, in_2);
  and and_39 (and_39_out, in_6, in_2);
  and and_40 (and_40_out, in_8, in_9);
  and and_41 (and_41_out, in_7, in_2);
  and and_42 (and_42_out, in_8, in_2);
  _7_adder u_7_adder_5 (
    .in_1(n7_adder_6_out_16), .in_2(and_40_out), .in_3(n7_adder_6_out_17), .in_4(and_37_out),
    .in_5(n7_adder_6_out_18), .in_6(and_34_out), .in_7(n7_adder_6_out_19), .in_8(and_31_out),
    .in_9(n7_adder_6_out_20), .in_10(and_30_out), .in_11(n7_adder_6_out_21), .in_12(and_27_out),
    .in_13(n7_adder_6_out_22), .in_14(and_22_out), .out_15(out_24), .out_16(n7_adder_5_out_16),
    .out_17(n7_adder_5_out_17), .out_18(n7_adder_5_out_18), .out_19(n7_adder_5_out_19),
    .out_20(n7_adder_5_out_20), .out_21(n7_adder_5_out_21), .out_22(n7_adder_5_out_22));
  and and_43 (and_43_out, 1'b1, in_1);
  not not_1 (not_1_out, 1'b1);
  and and_44 (and_44_out, in_3, in_1);
  _7_adder u_7_adder_6 (
    .in_1(and_48_out), .in_2(and_42_out), .in_3(and_47_out), .in_4(and_41_out), .in_5(and_45_out),
    .in_6(and_39_out), .in_7(and_46_out), .in_8(and_38_out), .in_9(and_44_out), .in_10(and_36_out),
    .in_11(and_43_out), .in_12(and_33_out), .in_13(not_1_out), .in_14(and_29_out), .out_15(out_25),
    .out_16(n7_adder_6_out_16), .out_17(n7_adder_6_out_17), .out_18(n7_adder_6_out_18),
    .out_19(n7_adder_6_out_19), .out_20(n7_adder_6_out_20), .out_21(n7_adder_6_out_21),
    .out_22(n7_adder_6_out_22));
  and and_45 (and_45_out, in_5, in_1);
  and and_46 (and_46_out, in_4, in_1);
  and and_47 (and_47_out, in_6, in_1);
  and and_48 (and_48_out, in_7, in_1);
  and and_49 (out_26, in_8, in_1);
endmodule

module mantissa2 (
  input  in_1,
  input  in_2,
  input  in_3,
  input  in_4,
  input  in_5,
  input  in_6,
  input  in_7,
  input  in_8,
  input  in_9,
  input  in_10,
  input  in_11,
  input  in_12,
  output out_13,
  output out_14,
  output out_15,
  output out_16,
  output out_17,
  output out_18,
  output out_19,
  output out_20,
  output out_21,
  output out_22,
  output out_23,
  output out_24,
  output out_25,
  output out_26,
  output out_27,
  output out_28
);

  wire and_1_out, and_2_out, and_3_out, and_4_out, and_5_out, and_6_out, and_7_out, and_8_out, and_9_out,
       and_10_out, and_11_out, and_12_out, and_13_out, and_14_out, and_15_out, and_16_out, and_17_out,
       and_18_out, and_19_out, and_20_out, and_21_out, and_22_out, and_23_out, and_24_out, and_25_out,
       and_26_out, and_27_out, and_28_out, and_29_out, and_30_out, and_31_out, and_32_out, and_33_out,
       and_34_out, and_35_out, half_adder_1_c, half_adder_1_s, half_adder_2_c, half_adder_2_s,
       half_adder_3_c, half_adder_3_s, n2_adder_1_out_5, n2_adder_1_out_6, n2_adder_1_out_7,
       n2_adder_2_out_5, n2_adder_2_out_6, n2_adder_2_out_7, n6_adder_2_out_14, n6_adder_2_out_15,
       n6_adder_2_out_16, n6_adder_2_out_17, n6_adder_2_out_18, n6_adder_2_out_19, n6_adder_3_out_14,
       n6_adder_3_out_15, n6_adder_3_out_16, n6_adder_3_out_17, n6_adder_3_out_18, n6_adder_3_out_19,
       n6_adder_4_out_14, n6_adder_4_out_15, n6_adder_4_out_16, n6_adder_4_out_17, n6_adder_4_out_18,
       n6_adder_4_out_19, n6_adder_5_out_14, n6_adder_5_out_15, n6_adder_5_out_16, n6_adder_5_out_17,
       n6_adder_5_out_18, n6_adder_5_out_19, not_1_out, not_2_out;

  and and_1 (and_1_out, in_3, in_12);
  and and_2 (and_2_out, in_5, in_12);
  and and_3 (and_3_out, in_4, in_12);
  and and_4 (and_4_out, in_3, in_11);
  and and_5 (and_5_out, in_6, in_12);
  not not_1 (not_1_out, 1'b1);
  and and_6 (and_6_out, in_4, in_11);
  and and_7 (and_7_out, in_5, in_11);
  and and_8 (and_8_out, in_7, in_12);
  Half_Adder half_adder_1 (.B(out_15), .A(out_14), .S(half_adder_1_s), .C(half_adder_1_c));
  _2_adder u_2_adder_1 (
    .in_1(half_adder_1_s), .in_2(out_13), .in_3(half_adder_1_c), .in_4(not_1_out), .out_5(n2_adder_1_out_5),
    .out_6(n2_adder_1_out_6), .out_7(n2_adder_1_out_7));
  and and_9 (and_9_out, in_3, in_10);
  and and_10 (and_10_out, in_6, in_11);
  and and_11 (and_11_out, in_8, in_12);
  Half_Adder half_adder_2 (.B(out_17), .A(out_16), .S(half_adder_2_s), .C(half_adder_2_c));
  _3_adder u_3_adder_1 (
    .in_1(n2_adder_2_out_5), .in_2(n2_adder_1_out_5), .in_3(n2_adder_2_out_6), .in_4(n2_adder_1_out_6),
    .in_5(n2_adder_2_out_7), .in_6(n2_adder_1_out_7), .out_7(out_28), .out_8(out_27), .out_9(out_26),
    .out_10(out_25));
  and and_12 (and_12_out, in_5, in_10);
  and and_13 (and_13_out, in_4, in_10);
  and and_14 (and_14_out, in_7, in_11);
  _6_adder u_6_adder_1 (
    .in_1(n6_adder_2_out_14), .in_2(n6_adder_2_out_15), .in_3(and_11_out), .in_4(and_8_out),
    .in_5(n6_adder_2_out_16), .in_6(and_5_out), .in_7(n6_adder_2_out_17), .in_8(and_2_out),
    .in_9(n6_adder_2_out_18), .in_10(and_3_out), .in_11(n6_adder_2_out_19), .in_12(and_1_out),
    .out_13(out_19), .out_14(out_18), .out_15(out_17), .out_16(out_16), .out_17(out_15), .out_18(out_14),
    .out_19(out_13));
  Half_Adder half_adder_3 (.B(out_19), .A(out_18), .S(half_adder_3_s), .C(half_adder_3_c));
  _2_adder u_2_adder_2 (
    .in_1(half_adder_3_s), .in_2(half_adder_2_s), .in_3(half_adder_3_c), .in_4(half_adder_2_c),
    .out_5(n2_adder_2_out_5), .out_6(n2_adder_2_out_6), .out_7(n2_adder_2_out_7));
  and and_15 (and_15_out, in_3, in_9);
  and and_16 (and_16_out, in_6, in_10);
  and and_17 (and_17_out, in_8, in_11);
  and and_18 (and_18_out, in_4, in_9);
  and and_19 (and_19_out, in_5, in_9);
  and and_20 (and_20_out, in_7, in_10);
  _6_adder u_6_adder_2 (
    .in_1(n6_adder_3_out_14), .in_2(n6_adder_3_out_15), .in_3(and_17_out), .in_4(and_14_out),
    .in_5(n6_adder_3_out_16), .in_6(and_10_out), .in_7(n6_adder_3_out_17), .in_8(and_7_out),
    .in_9(n6_adder_3_out_18), .in_10(and_6_out), .in_11(n6_adder_3_out_19), .in_12(and_4_out),
    .out_13(out_20), .out_14(n6_adder_2_out_14), .out_15(n6_adder_2_out_15), .out_16(n6_adder_2_out_16),
    .out_17(n6_adder_2_out_17), .out_18(n6_adder_2_out_18), .out_19(n6_adder_2_out_19));
  and and_21 (and_21_out, in_3, in_1);
  and and_22 (and_22_out, in_6, in_9);
  and and_23 (and_23_out, in_8, in_10);
  and and_24 (and_24_out, in_5, in_1);
  and and_25 (and_25_out, in_4, in_1);
  and and_26 (and_26_out, in_7, in_9);
  _6_adder u_6_adder_3 (
    .in_1(n6_adder_4_out_14), .in_2(n6_adder_4_out_15), .in_3(and_23_out), .in_4(and_20_out),
    .in_5(n6_adder_4_out_16), .in_6(and_16_out), .in_7(n6_adder_4_out_17), .in_8(and_12_out),
    .in_9(n6_adder_4_out_18), .in_10(and_13_out), .in_11(n6_adder_4_out_19), .in_12(and_9_out),
    .out_13(out_21), .out_14(n6_adder_3_out_14), .out_15(n6_adder_3_out_15), .out_16(n6_adder_3_out_16),
    .out_17(n6_adder_3_out_17), .out_18(n6_adder_3_out_18), .out_19(n6_adder_3_out_19));
  and and_27 (and_27_out, in_6, in_1);
  and and_28 (and_28_out, in_8, in_9);
  and and_29 (and_29_out, in_7, in_1);
  _6_adder u_6_adder_4 (
    .in_1(n6_adder_5_out_14), .in_2(n6_adder_5_out_15), .in_3(and_28_out), .in_4(and_26_out),
    .in_5(n6_adder_5_out_16), .in_6(and_22_out), .in_7(n6_adder_5_out_17), .in_8(and_19_out),
    .in_9(n6_adder_5_out_18), .in_10(and_18_out), .in_11(n6_adder_5_out_19), .in_12(and_15_out),
    .out_13(out_22), .out_14(n6_adder_4_out_14), .out_15(n6_adder_4_out_15), .out_16(n6_adder_4_out_16),
    .out_17(n6_adder_4_out_17), .out_18(n6_adder_4_out_18), .out_19(n6_adder_4_out_19));
  and and_30 (and_30_out, in_8, in_1);
  not not_2 (not_2_out, 1'b1);
  and and_31 (and_31_out, in_3, in_2);
  _6_adder u_6_adder_5 (
    .in_1(and_35_out), .in_2(and_33_out), .in_3(and_30_out), .in_4(and_29_out), .in_5(and_34_out),
    .in_6(and_27_out), .in_7(and_32_out), .in_8(and_24_out), .in_9(and_31_out), .in_10(and_25_out),
    .in_11(not_2_out), .in_12(and_21_out), .out_13(out_23), .out_14(n6_adder_5_out_14),
    .out_15(n6_adder_5_out_15), .out_16(n6_adder_5_out_16), .out_17(n6_adder_5_out_17),
    .out_18(n6_adder_5_out_18), .out_19(n6_adder_5_out_19));
  and and_32 (and_32_out, in_4, in_2);
  and and_33 (and_33_out, in_6, in_2);
  and and_34 (and_34_out, in_5, in_2);
  and and_35 (and_35_out, in_7, in_2);
  and and_36 (out_24, in_8, in_2);
endmodule

module exponent (
  input  C0,
  input  A0,
  input  A1,
  input  B0,
  input  A2,
  input  B1,
  input  B2,
  input  A3,
  input  B3,
  input  A4,
  input  A5,
  input  B4,
  input  A6,
  input  B5,
  input  B6,
  input  A7,
  input  B7,
  output S0,
  output S1,
  output S2,
  output S3,
  output S4,
  output S5,
  output S6,
  output S7,
  output C
);

  wire and_1_out, full_adder_1_c_2, full_adder_1_s, full_adder_2_c_2, full_adder_2_s, full_adder_3_c_2,
       full_adder_3_s, full_adder_4_c_2, full_adder_4_s, full_adder_5_c_2, full_adder_5_s, full_adder_6_c_2,
       full_adder_6_s, full_adder_7_c_2, full_adder_7_s, full_adder_8_c_2, full_adder_8_s, full_adder_9_s,
       half_adder_1_c, half_adder_1_s, half_adder_2_c, half_adder_2_s, half_adder_3_c, half_adder_3_s,
       half_adder_4_c, half_adder_4_s, half_adder_5_c, half_adder_5_s, half_adder_6_c, half_adder_6_s,
       half_adder_7_c, half_adder_7_s, not_1_out;

  Half_Adder half_adder_1 (.B(1'b1), .A(B0), .S(half_adder_1_s), .C(half_adder_1_c));
  Half_Adder half_adder_2 (.B(half_adder_1_c), .A(B1), .S(half_adder_2_s), .C(half_adder_2_c));
  Full_Adder full_adder_1 (.B(A0), .A(half_adder_1_s), .C(C0), .S(full_adder_1_s), .C_2(full_adder_1_c_2));
  Half_Adder half_adder_3 (.B(half_adder_2_c), .A(B2), .S(half_adder_3_s), .C(half_adder_3_c));
  Full_Adder full_adder_2 (
    .B(A1), .A(half_adder_2_s), .C(full_adder_1_c_2), .S(full_adder_2_s), .C_2(full_adder_2_c_2));
  Half_Adder half_adder_4 (.B(half_adder_3_c), .A(B3), .S(half_adder_4_s), .C(half_adder_4_c));
  Half_Adder half_adder_5 (.B(half_adder_4_c), .A(B4), .S(half_adder_5_s), .C(half_adder_5_c));
  Full_Adder full_adder_3 (
    .B(A2), .A(half_adder_3_s), .C(full_adder_2_c_2), .S(full_adder_3_s), .C_2(full_adder_3_c_2));
  Half_Adder half_adder_6 (.B(half_adder_5_c), .A(B5), .S(half_adder_6_s), .C(half_adder_6_c));
  Full_Adder full_adder_4 (
    .B(A3), .A(half_adder_4_s), .C(full_adder_3_c_2), .S(full_adder_4_s), .C_2(full_adder_4_c_2));
  Half_Adder half_adder_7 (.B(half_adder_6_c), .A(B6), .S(half_adder_7_s), .C(half_adder_7_c));
  Full_Adder full_adder_5 (
    .B(A4), .A(half_adder_5_s), .C(full_adder_4_c_2), .S(full_adder_5_s), .C_2(full_adder_5_c_2));
  Full_Adder full_adder_6 (.B(B7), .A(1'b1), .C(half_adder_7_c), .S(full_adder_6_s), .C_2(full_adder_6_c_2));
  Full_Adder full_adder_7 (
    .B(A5), .A(half_adder_6_s), .C(full_adder_5_c_2), .S(full_adder_7_s), .C_2(full_adder_7_c_2));
  Full_Adder full_adder_8 (
    .B(A6), .A(half_adder_7_s), .C(full_adder_7_c_2), .S(full_adder_8_s), .C_2(full_adder_8_c_2));
  Full_Adder full_adder_9 (.B(A7), .A(full_adder_6_s), .C(full_adder_8_c_2), .S(full_adder_9_s), .C_2(C));
  not not_1 (not_1_out, and_1_out);
  and and_1 (and_1_out, full_adder_9_s, full_adder_6_c_2);
  nand nand_1 (S0, full_adder_1_s, not_1_out);
  nand nand_2 (S1, full_adder_2_s, not_1_out);
  nand nand_3 (S2, full_adder_3_s, not_1_out);
  nand nand_4 (S3, full_adder_4_s, not_1_out);
  nand nand_5 (S4, full_adder_5_s, not_1_out);
  nand nand_6 (S5, full_adder_7_s, not_1_out);
  nand nand_7 (S6, full_adder_8_s, not_1_out);
  nand nand_8 (S7, full_adder_9_s, not_1_out);
endmodule

module Half_Adder (
  input  B,
  input  A,
  output S,
  output C
);

  xor xor_1 (S, B, A);
  and and_1 (C, B, A);
endmodule

module Full_Adder (
  input  B,
  input  A,
  input  C,
  output S,
  output C_2
);

  wire and_1_out, and_2_out, xor_1_out;

  xor xor_1 (xor_1_out, B, A);
  and and_1 (and_1_out, xor_1_out, C);
  and and_2 (and_2_out, B, A);
  xor xor_2 (S, xor_1_out, C);
  or or_1 (C_2, and_1_out, and_2_out);
endmodule

module _2_adder (
  input  in_1,
  input  in_2,
  input  in_3,
  input  in_4,
  output out_5,
  output out_6,
  output out_7
);

  wire half_adder_1_c;

  Half_Adder half_adder_1 (.B(in_1), .A(in_2), .S(out_5), .C(half_adder_1_c));
  Full_Adder full_adder_1 (.B(in_3), .A(in_4), .C(half_adder_1_c), .S(out_6), .C_2(out_7));
endmodule

module _3_adder (
  input  in_1,
  input  in_2,
  input  in_3,
  input  in_4,
  input  in_5,
  input  in_6,
  output out_7,
  output out_8,
  output out_9,
  output out_10
);

  wire full_adder_1_c_2, half_adder_1_c;

  Half_Adder half_adder_1 (.B(in_1), .A(in_2), .S(out_7), .C(half_adder_1_c));
  Full_Adder full_adder_1 (.B(in_3), .A(in_4), .C(half_adder_1_c), .S(out_8), .C_2(full_adder_1_c_2));
  Full_Adder full_adder_2 (.B(in_5), .A(in_6), .C(full_adder_1_c_2), .S(out_9), .C_2(out_10));
endmodule

module _6_adder (
  input  in_1,
  input  in_2,
  input  in_3,
  input  in_4,
  input  in_5,
  input  in_6,
  input  in_7,
  input  in_8,
  input  in_9,
  input  in_10,
  input  in_11,
  input  in_12,
  output out_13,
  output out_14,
  output out_15,
  output out_16,
  output out_17,
  output out_18,
  output out_19
);

  wire and_1_out, and_2_out, and_3_out, and_4_out, and_5_out, and_6_out, and_7_out, and_8_out, and_9_out,
       and_10_out, and_11_out, or_1_out, or_2_out, or_3_out, or_4_out, xor_2_out, xor_4_out, xor_6_out,
       xor_8_out, xor_10_out;

  xor xor_1 (out_13, in_1, in_3);
  xor xor_2 (xor_2_out, in_7, in_8);
  and and_1 (and_1_out, in_1, in_3);
  and and_2 (and_2_out, xor_2_out, or_4_out);
  and and_3 (and_3_out, in_7, in_8);
  xor xor_3 (out_16, xor_2_out, or_4_out);
  xor xor_4 (xor_4_out, in_2, in_4);
  and and_4 (and_4_out, in_2, in_4);
  or or_1 (or_1_out, and_2_out, and_3_out);
  and and_5 (and_5_out, xor_4_out, and_1_out);
  xor xor_5 (out_14, xor_4_out, and_1_out);
  xor xor_6 (xor_6_out, in_9, in_10);
  and and_6 (and_6_out, in_9, in_10);
  or or_2 (or_2_out, and_5_out, and_4_out);
  xor xor_7 (out_17, xor_6_out, or_1_out);
  and and_7 (and_7_out, xor_6_out, or_1_out);
  or or_3 (or_3_out, and_7_out, and_6_out);
  xor xor_8 (xor_8_out, in_5, in_6);
  and and_8 (and_8_out, in_5, in_6);
  xor xor_9 (out_15, xor_8_out, or_2_out);
  and and_9 (and_9_out, xor_8_out, or_2_out);
  xor xor_10 (xor_10_out, in_11, in_12);
  or or_4 (or_4_out, and_9_out, and_8_out);
  and and_10 (and_10_out, xor_10_out, or_3_out);
  and and_11 (and_11_out, in_11, in_12);
  xor xor_11 (out_18, xor_10_out, or_3_out);
  or or_5 (out_19, and_10_out, and_11_out);
endmodule

module _7_adder (
  input  in_1,
  input  in_2,
  input  in_3,
  input  in_4,
  input  in_5,
  input  in_6,
  input  in_7,
  input  in_8,
  input  in_9,
  input  in_10,
  input  in_11,
  input  in_12,
  input  in_13,
  input  in_14,
  output out_15,
  output out_16,
  output out_17,
  output out_18,
  output out_19,
  output out_20,
  output out_21,
  output out_22
);

  wire full_adder_1_c_2, full_adder_2_c_2, full_adder_3_c_2, full_adder_4_c_2, full_adder_5_c_2,
       half_adder_1_c;

  Half_Adder half_adder_1 (.B(in_1), .A(in_2), .S(out_15), .C(half_adder_1_c));
  Full_Adder full_adder_1 (.B(in_3), .A(in_4), .C(half_adder_1_c), .S(out_16), .C_2(full_adder_1_c_2));
  Full_Adder full_adder_2 (.B(in_5), .A(in_6), .C(full_adder_1_c_2), .S(out_17), .C_2(full_adder_2_c_2));
  Full_Adder full_adder_3 (.B(in_7), .A(in_8), .C(full_adder_2_c_2), .S(out_18), .C_2(full_adder_3_c_2));
  Full_Adder full_adder_4 (.B(in_9), .A(in_10), .C(full_adder_3_c_2), .S(out_19), .C_2(full_adder_4_c_2));
  Full_Adder full_adder_5 (.B(in_11), .A(in_12), .C(full_adder_4_c_2), .S(out_20), .C_2(full_adder_5_c_2));
  Full_Adder full_adder_6 (.B(in_13), .A(in_14), .C(full_adder_5_c_2), .S(out_21), .C_2(out_22));
endmodule

module shift (
  input  Clock,
  input  _12,
  input  _11,
  input  _10,
  input  _9,
  input  _8,
  input  _7,
  input  _6,
  input  _5,
  input  _4,
  input  _3,
  input  _2,
  input  _1,
  input  _0,
  input  in_15,
  input  Reset,
  output out_17,
  output out_18,
  output out_19,
  output out_20,
  output out_21,
  output out_22,
  output out_23,
  output out_24,
  output out_25,
  output out_26,
  output out_27,
  output out_28
);

  wire and_1_out, and_2_out, and_3_out, and_4_out, and_5_out, and_6_out, and_7_out, and_8_out, and_9_out,
       and_10_out, and_11_out, and_12_out, and_13_out, and_14_out, and_15_out, and_16_out, and_17_out,
       and_18_out, and_19_out, and_20_out, and_21_out, and_22_out, and_23_out, and_24_out, and_25_out,
       d_ff_1_q, d_ff_2_q, d_ff_3_q, not_1_out, or_1_out, or_2_out, or_3_out, or_4_out, or_5_out, or_6_out,
       or_7_out, or_8_out, or_9_out, or_10_out, or_11_out, or_12_out, or_13_out;

  D_Flip_Flop d_ff_1 (.clk(Clock), .D(in_15), .Q(d_ff_1_q), .reset(Reset));  // open: Qn, preset, en
  D_Flip_Flop d_ff_2 (.clk(Clock), .D(d_ff_1_q), .Q(d_ff_2_q), .reset(Reset));  // open: Qn, preset, en
  or or_1 (or_1_out, Clock, d_ff_2_q);
  not not_1 (not_1_out, d_ff_1_q);
  and and_1 (and_1_out, _12, not_1_out);
  D_Flip_Flop d_ff_3 (.clk(or_1_out), .D(and_1_out), .Q(d_ff_3_q), .reset(Reset));  // open: Qn, preset, en
  and and_2 (and_2_out, d_ff_3_q, d_ff_1_q);
  and and_3 (and_3_out, _11, not_1_out);
  or or_2 (or_2_out, and_2_out, and_3_out);
  D_Flip_Flop d_ff_4 (.clk(or_1_out), .D(or_2_out), .Q(out_17), .reset(Reset));  // open: Qn, preset, en
  and and_4 (and_4_out, out_17, d_ff_1_q);
  and and_5 (and_5_out, _10, not_1_out);
  or or_3 (or_3_out, and_4_out, and_5_out);
  D_Flip_Flop d_ff_5 (.clk(or_1_out), .D(or_3_out), .Q(out_18), .reset(Reset));  // open: Qn, preset, en
  and and_6 (and_6_out, out_18, d_ff_1_q);
  or or_4 (or_4_out, and_6_out, and_7_out);
  and and_7 (and_7_out, _9, not_1_out);
  D_Flip_Flop d_ff_6 (.clk(or_1_out), .D(or_4_out), .Q(out_19), .reset(Reset));  // open: Qn, preset, en
  and and_8 (and_8_out, out_19, d_ff_1_q);
  and and_9 (and_9_out, _8, not_1_out);
  or or_5 (or_5_out, and_8_out, and_9_out);
  D_Flip_Flop d_ff_7 (.clk(or_1_out), .D(or_5_out), .Q(out_20), .reset(Reset));  // open: Qn, preset, en
  and and_10 (and_10_out, out_20, d_ff_1_q);
  and and_11 (and_11_out, _7, not_1_out);
  or or_6 (or_6_out, and_10_out, and_11_out);
  D_Flip_Flop d_ff_8 (.clk(or_1_out), .D(or_6_out), .Q(out_21), .reset(Reset));  // open: Qn, preset, en
  and and_12 (and_12_out, out_21, d_ff_1_q);
  and and_13 (and_13_out, _6, not_1_out);
  or or_7 (or_7_out, and_12_out, and_13_out);
  D_Flip_Flop d_ff_9 (.clk(or_1_out), .D(or_7_out), .Q(out_22), .reset(Reset));  // open: Qn, preset, en
  and and_14 (and_14_out, out_22, d_ff_1_q);
  and and_15 (and_15_out, _5, not_1_out);
  or or_8 (or_8_out, and_14_out, and_15_out);
  D_Flip_Flop d_ff_10 (.clk(or_1_out), .D(or_8_out), .Q(out_23), .reset(Reset));  // open: Qn, preset, en
  and and_16 (and_16_out, out_23, d_ff_1_q);
  and and_17 (and_17_out, _4, not_1_out);
  or or_9 (or_9_out, and_16_out, and_17_out);
  D_Flip_Flop d_ff_11 (.clk(or_1_out), .D(or_9_out), .Q(out_24), .reset(Reset));  // open: Qn, preset, en
  and and_18 (and_18_out, out_24, d_ff_1_q);
  and and_19 (and_19_out, _3, not_1_out);
  or or_10 (or_10_out, and_18_out, and_19_out);
  D_Flip_Flop d_ff_12 (.clk(or_1_out), .D(or_10_out), .Q(out_25), .reset(Reset));  // open: Qn, preset, en
  and and_20 (and_20_out, out_25, d_ff_1_q);
  and and_21 (and_21_out, _2, not_1_out);
  or or_11 (or_11_out, and_20_out, and_21_out);
  D_Flip_Flop d_ff_13 (.clk(or_1_out), .D(or_11_out), .Q(out_26), .reset(Reset));  // open: Qn, preset, en
  and and_22 (and_22_out, out_26, d_ff_1_q);
  or or_12 (or_12_out, and_22_out, and_23_out);
  and and_23 (and_23_out, _1, not_1_out);
  D_Flip_Flop d_ff_14 (.clk(or_1_out), .D(or_12_out), .Q(out_27), .reset(Reset));  // open: Qn, preset, en
  and and_24 (and_24_out, out_27, d_ff_1_q);
  and and_25 (and_25_out, _0, not_1_out);
  or or_13 (or_13_out, and_24_out, and_25_out);
  D_Flip_Flop d_ff_15 (.clk(or_1_out), .D(or_13_out), .Q(out_28));  // open: Qn, preset, en, reset

  // Notes on the sheet:
  //   13最高位(決定是否移位)
endmodule
